# Fritzing sketch schematic (saved by Fritzing 0.9.4)
breadboards: 1

parts:
  HARP_ADAPTER = Arduino Uno (Rev3)
  HARP_IN = DIN-5 jack (MIDI) [package=THT]

nets:
  N1: HARP_ADAPTER.D8, HARP_IN.2
  N2: HARP_ADAPTER.GND, HARP_IN.3
  N3: HARP_ADAPTER.D2, HARP_IN.5
  N4: HARP_ADAPTER.D3_PWM, HARP_IN.1
  N5: HARP_ADAPTER.5V, HARP_IN.4
