# Fritzing sketch nano-schematic (saved by Fritzing 0.9.4)
circuit board: 9.01339cm x 10.0303cm
breadboards: 1

parts:
  HARP_IN = DIN-5 jack (MIDI) [package=THT]
  MIDI_OUT = DIN-5 jack (MIDI) [package=THT]
  R1 = Resistor [tolerance=±5% resistance=220 package=THT]
  Arduino = Arduino Nano (Rev3.0)
  R2 = Resistor [tolerance=±5% resistance=100k package=THT]

nets:
  N1: HARP_IN.3, Arduino.D2
  N2: HARP_IN.5, Arduino.D3, R2.Pin_1
  N3: HARP_IN.2, MIDI_OUT.2, Arduino.GND, R2.Pin_0
  N4: HARP_IN.4, R1.Pin_0, Arduino.5V
  N5: HARP_IN.1, Arduino.D8
  N6: MIDI_OUT.5, Arduino.D4
  N7: MIDI_OUT.4, R1.Pin_1
