# Fritzing sketch schematic (saved by Fritzing 0.9.4)
breadboards: 1

parts:
  HARP_ADAPTER = Arduino Uno (Rev3)
  HARP_IN = DIN-5 jack (MIDI) [package=THT]
  MIDI_OUT = DIN-5 jack (MIDI) [package=THT]
  R1 = Resistor [tolerance=±5% resistance=220 package=THT]

nets:
  N1: HARP_ADAPTER.D8, HARP_IN.5
  N2: HARP_ADAPTER.D11_PWM/MOSI, MIDI_OUT.5
  N3: HARP_ADAPTER.GND, HARP_IN.2, MIDI_OUT.2
  N4: HARP_ADAPTER.D2, HARP_IN.1
  N5: HARP_ADAPTER.D3_PWM, HARP_IN.3
  N6: HARP_ADAPTER.5V, HARP_IN.4, R1.Pin_1
  N7: MIDI_OUT.4, R1.Pin_0
